# Fritzing sketch Encoder and 4 digit to D1 mini + I2C to RPI (saved by Fritzing 1.0.0rc)
breadboards: 1

parts:
  WeMos_D1_Mini1 = WeMos D1 Mini
  Rotary_encoder = IC, SIP package, 4 pins
  4-digit_display = IC, SIP package, 4 pins
  Mod1 = Raspberry Pi 4B
  R1 = Resistor [tolerance=±5% power=0.25W resistance=4700 package=THT]
  R2 = Resistor [tolerance=±5% power=0.25W resistance=4700 package=THT]

nets:
  N1: WeMos_D1_Mini1.3V3, Rotary_encoder.pin1
  N2: WeMos_D1_Mini1.5V, 4-digit_display.pin2
  N3: WeMos_D1_Mini1.D1, Mod1.GPIO3, R1.Pin_0
  N4: WeMos_D1_Mini1.D2, Mod1.GPIO2, R2.Pin_0
  N5: WeMos_D1_Mini1.D3, 4-digit_display.pin4
  N6: WeMos_D1_Mini1.D4, 4-digit_display.pin3
  N7: WeMos_D1_Mini1.D5, Rotary_encoder.pin3
  N8: WeMos_D1_Mini1.D6, Rotary_encoder.pin4
  N9: WeMos_D1_Mini1.G, Rotary_encoder.pin2, 4-digit_display.pin1, Mod1.GND
  N10: Mod1.3V3, R1.Pin_1, R2.Pin_1
