# Fritzing sketch Encoder to D1 mini (saved by Fritzing 1.0.0rc)
breadboards: 1

parts:
  WeMos_D1_Mini1 = WeMos D1 Mini
  Rotary_encoder = IC, SIP package, 4 pins

nets:
  N1: WeMos_D1_Mini1.3V3, Rotary_encoder.pin1
  N2: WeMos_D1_Mini1.D5, Rotary_encoder.pin3
  N3: WeMos_D1_Mini1.D6, Rotary_encoder.pin4
  N4: WeMos_D1_Mini1.G, Rotary_encoder.pin2
