# Fritzing sketch Encoder with button and 4 digit to D1 mini (saved by Fritzing 1.0.0rc)
breadboards: 1

parts:
  WeMos_D1_Mini1 = WeMos D1 Mini
  4-digit_display = IC, SIP package, 4 pins
  Rotary_encoder_with_button = IC, SIP package, 5 pins

nets:
  N1: WeMos_D1_Mini1.3V3, Rotary_encoder_with_button.pin1
  N2: WeMos_D1_Mini1.5V, 4-digit_display.pin2
  N3: WeMos_D1_Mini1.D1, 4-digit_display.pin4
  N4: WeMos_D1_Mini1.D2, 4-digit_display.pin3
  N5: WeMos_D1_Mini1.D5, Rotary_encoder_with_button.pin3
  N6: WeMos_D1_Mini1.D6, Rotary_encoder_with_button.pin4
  N7: WeMos_D1_Mini1.D7, Rotary_encoder_with_button.pin5
  N8: WeMos_D1_Mini1.G, 4-digit_display.pin1, Rotary_encoder_with_button.pin2
